# Fritzing sketch drumcore (saved by Fritzing 1.0.8)

parts:
  A1 = ESP32-S3-WROOM-1-N16R8 dev board
  Componente1 = Analog Digital MUX Breakout
  Componente2 = Analog Digital MUX Breakout
  LCD1 = TFT 1.8 inch 160x128 w SD
  RE1 = KY-040 Rotary encoder [package=THT]

nets:
  VCC: A1.Pin_1, A1.Pin_2, Componente1.VCC, Componente2.VCC, LCD1.Pin_7, RE1.VCC
  N1: A1.Pin_4, RE1.S1
  N2: A1.Pin_5, RE1.S2
  N3: A1.Pin_6, RE1.KEY
  N4: A1.Pin_7, LCD1.Pin_6
  N5: A1.Pin_8, LCD1.Pin_5
  N6: A1.Pin_9, LCD1.Pin_4
  N7: A1.Pin_10, LCD1.Pin_3
  N8: A1.Pin_11, LCD1.Pin_2
  N9: A1.Pin_12, LCD1.Pin_1
  GND: A1.Pin_22, A1.Pin_23, A1.Pin_44, Componente1.GND, Componente2.GND, LCD1.Pin_8, RE1.GND
  N10: A1.Pin_36, Componente2.SIG
  N11: A1.Pin_37, Componente1.SIG
  N12: A1.Pin_38, Componente1.S3, Componente2.S3
  N13: A1.Pin_39, Componente1.S2, Componente2.S2
  N14: A1.Pin_40, Componente1.S1, Componente2.S1
  N15: A1.Pin_41, Componente1.S0, Componente2.S0

custom parts:
  ESP32-S3-WROOM-1-N16R8 dev board: ESP32-S3 WIFI+BLE5.0 Development Board ESP32-S3-WROOM-1-N16R8(16M Flash/8SRAM).
  TFT 1.8 inch 160x128 w SD: This is a generic 1.8 tft spi lcd display available on ebay and others. The 1.8" display has 128x160 color pixels and in this version pin names in breadboard (unlike the real board).
  KY-040 Rotary encoder: KY-040 Rotary Encoder with switch on breakout borad from AZ Delivery
